# Fritzing sketch circuito_pick_and_place (saved by Fritzing 0.9.3b)

parts:
  Componente1 = Arduino Uno (Rev3)  # not connected
  Arduino_CNC_Shield_V3_00_1 = Arduino_CNC_V3.00
  J1 = Basic Servo
  JL012-13-5_1 = JL012-13-5.2 Lever (Limit) Switch SPDT + NO + NC [part_number=JL012-13-5.2]
  JL012-13-5_2 = JL012-13-5.2 Lever (Limit) Switch SPDT + NO + NC [part_number=JL012-13-5.2]
  V1 = DC Power [voltage=12V]  # not connected
  M5 = 1 chan 5v relay module
  L1 = Solenoid
  M6 = Stepper Motor - Bipolar
  M8 = Stepper Motor - Bipolar
  M9 = Stepper Motor - Bipolar

nets:
  N1: Arduino_CNC_Shield_V3_00_1.X-MTR_'1', M6.A
  N2: Arduino_CNC_Shield_V3_00_1.X-MTR_'2', M6.C
  N3: Arduino_CNC_Shield_V3_00_1.X-MTR_'3', M6.B
  N4: Arduino_CNC_Shield_V3_00_1.X-MTR_'4', M6.D
  N5: Arduino_CNC_Shield_V3_00_1.Y-MTR_'1', M9.D
  N6: Arduino_CNC_Shield_V3_00_1.Y-MTR_'2', M9.B
  N7: Arduino_CNC_Shield_V3_00_1.Y-MTR_'3', M9.C
  N8: Arduino_CNC_Shield_V3_00_1.Y-MTR_'4', M9.A
  N9: Arduino_CNC_Shield_V3_00_1.A-MTR_'1', M8.A
  N10: Arduino_CNC_Shield_V3_00_1.A-MTR_'2', M8.C
  N11: Arduino_CNC_Shield_V3_00_1.A-MTR_'3', M8.B
  N12: Arduino_CNC_Shield_V3_00_1.A-MTR_'4', M8.D
  5V: Arduino_CNC_Shield_V3_00_1.5V, J1.vcc, M5.pin_1
  N13: Arduino_CNC_Shield_V3_00_1.End_Stops_Z+_(Gnd), JL012-13-5_2.NC
  N14: Arduino_CNC_Shield_V3_00_1.End_Stops_Z-_(Gnd), L1.pin1
  N15: Arduino_CNC_Shield_V3_00_1.End_Stops_Y-_(and_Y+), JL012-13-5_2.C
  N16: Arduino_CNC_Shield_V3_00_1.End_Stops_X+_(Gnd), JL012-13-5_1.NC, M5.pin_2
  N17: Arduino_CNC_Shield_V3_00_1.End_Stops_X-_(and_X+), JL012-13-5_1.C
  N18: Arduino_CNC_Shield_V3_00_1.SpnEn_/_Z_Limit, M5.pin_3
  N19: Arduino_CNC_Shield_V3_00_1.SpnDir, J1.pulse
  N20: Arduino_CNC_Shield_V3_00_1.E-STOP_(Gnd), J1.gnd
  N21: M5.pin_5, L1.pin2

notes:
  Servo eixo X
  Servo eixo Y
  Chave de final de curso do eixo Y e X
  Eletroimã

custom parts:
  Arduino_CNC_V3.00: Protoneer Arduino CNC Shield V3.00 If using Grbl V0.9: The “A” axis can not be used (yet). The “SCL” (Arduino A5) pin is now used for 'Probing' input. The “End Stops Z+ & Z-” (Arduino D11) and “SpnEn” (Arduino D12) have been switched!
  JL012-13-5.2 Lever (Limit) Switch SPDT + NO + NC: Micro Switch; Model No.: JL012-13.5-2; Actuator Action: Momentary; Actuator Type: Hinge Lever; Contact Configuration: 1NO, 1NC (SPDT) Temperature -25~65℃；Relative humidity: below 85%; Rate Voltage: 125V AC; Rated Current: 1A.
  1 chan 5v relay module: 1 Channel 5V Relay Module Board Shield with Optocoupler Support High and Low Level Trigger for Arduino.
